# Fritzing sketch seed_board (saved by Fritzing 0.9.3b)
circuit board: 8.46667cm x 5.64444cm
breadboards: 1

parts:
  S1 = Reed switch [package=THT]
  S2 = Reed switch [package=THT]
  S3 = Reed switch [package=THT]
  S4 = Reed switch [package=THT]
  S5 = Reed switch [package=THT]
  S6 = Reed switch [package=THT]
  J2 = shrouded pin header, 10 pins [form="♂ (shrouded male)"]
  S7 = Reed switch [package=THT]
  S8 = Reed switch [package=THT]
  S9 = Reed switch [package=THT]
  S10 = Reed switch [package=THT]
  S11 = Reed switch [package=THT]
  S12 = Reed switch [package=THT]
  S13 = Reed switch [package=THT]
  S14 = Reed switch [package=THT]
  S15 = Reed switch [package=THT]
  J1 = shrouded pin header, 10 pins [form="♂ (shrouded male)"]

nets:
  N1: S1.pin_1, S2.pin_1, S3.pin_1, S4.pin_1, S5.pin_1, S6.pin_1
  N2: S1.pin_2, S7.pin_1, J1.pin1, J1.pin10
  N3: S2.pin_2, S8.pin_1, J1.pin2, J1.pin9
  N4: S3.pin_2, S9.pin_1, J1.pin3, J1.pin8
  N5: S4.pin_2, J2.pin1, J2.pin10, S12.pin_1
  N6: S5.pin_2, J2.pin3, J2.pin8
  N7: S6.pin_2, J2.pin5, J2.pin6
  N8: J2.pin2, J2.pin9, S13.pin_1
  N9: J2.pin4, J2.pin7, S14.pin_1
  N10: S7.pin_2, S8.pin_2, S9.pin_2, S10.pin_2, S11.pin_2, S12.pin_2, S13.pin_2, S14.pin_2, S15.pin_2
  N11: S10.pin_1, J1.pin4, J1.pin7
  N12: S11.pin_1, J1.pin5, J1.pin6

notes:
  This represents the cobbler. Look at code for actual input pins.
